// Logisim project CPU_V1.circ as structural Verilog: 8 circuits, main circuit main
module main (
);

  wire button_1_out, clock_1_out, not_1_out, uc_1_read, uc_1_wpc, uc_1_write;
  wire [2:0] uc_1_function_sel;
  wire [3:0] alu_4_1_out_4, dsel_1_out, main_1_dbga, main_1_dbgb, main_1_dbgc, main_1_dbgd, main_1_xout,
       main_1_yout, pc_1_out_2, ram_1_data, uc_1_mad, uc_1_out_5, uc_1_pcout, uc_1_rx, uc_1_ry;
  wire [11:0] rom_1_data;

  Button button_1 (.out(button_1_out));
  ROM #(.addrWidth(4), .dataWidth(12)) rom_1 (.addr(pc_1_out_2), .data(rom_1_data), .sel(1'b1));
  // Probe on main_1_dbga
  // Probe on main_1_dbgb
  dSel dsel_1 (.ALUIn(alu_4_1_out_4), .RAMIn(ram_1_data), .Out(dsel_1_out), .Sel(uc_1_read));
  UC uc_1 (
    .RI_In(rom_1_data), .RESET(button_1_out), .read(uc_1_read), .function_sel(uc_1_function_sel),
    .PCIn(pc_1_out_2), .PCOut(uc_1_pcout), .wPC(uc_1_wpc), .mAD(uc_1_mad), .write(uc_1_write),
    .out_5(uc_1_out_5), .rX(uc_1_rx), .rY(uc_1_ry));  // open: RI_Out
  PC pc_1 (.In(uc_1_pcout), .out_2(pc_1_out_2));
  // Probe on main_1_dbgd
  // Probe on main_1_dbgc
  RegFile_main main_1 (
    .dIn(dsel_1_out), .wSel(uc_1_out_5), .XOut(main_1_xout), .YOut(main_1_yout), .XSel(uc_1_rx),
    .YSel(uc_1_ry), .dbgA(main_1_dbga), .dbgB(main_1_dbgb), .dbgC(main_1_dbgc), .dbgD(main_1_dbgd));
  // Probe on main_1_yout
  // Probe on uc_1_function_sel
  ALU_4 alu_4_1 (.a(main_1_yout), .b(main_1_xout), .out_4(alu_4_1_out_4), .sel(uc_1_function_sel));  // open: Carry_out
  // Probe on main_1_xout
  Clock clock_1 (.out(clock_1_out));
  // Probe on alu_4_1_out_4
  RAM #(.addrWidth(4), .dataWidth(4), .bus("separate")) ram_1 (
    .addr(uc_1_mad), .din(alu_4_1_out_4), .data(ram_1_data), .str(uc_1_write), .sel(1'b1), .clk(clock_1_out),
    .ld(not_1_out), .clr(1'b0));
  not not_1 (not_1_out, uc_1_write);
  // Probe on ram_1_data

  // Notes on the sheet:
  //   contents of rom_1 (hex, n*v repeats v):
  //   400 444 84 888 184 88c
endmodule

module XOR (
  input  a,
  input  b,
  output S
);

  wire and_1_out, and_2_out, not_1_out, not_2_out;

  not not_1 (not_1_out, b);
  not not_2 (not_2_out, a);
  and and_1 (and_1_out, not_1_out, a);
  and and_2 (and_2_out, not_2_out, b);
  or or_1 (S, and_1_out, and_2_out);
endmodule

module HalfAdder (
  input  a,
  input  b,
  output Result,
  output Carry_out
);

  XOR xor_1 (.a(b), .S(Result), .b(a));
  and and_1 (Carry_out, b, a);
endmodule

module FullAdder (
  input  Carry_in,
  input  a,
  input  b,
  output S,
  output Carry_out
);

  wire halfadder_1_carry_out, halfadder_1_result, halfadder_2_carry_out;

  HalfAdder halfadder_1 (.Result(halfadder_1_result), .Carry_out(halfadder_1_carry_out), .a(b), .b(a));
  HalfAdder halfadder_2 (.Result(S), .Carry_out(halfadder_2_carry_out), .a(halfadder_1_result), .b(Carry_in));
  or or_1 (Carry_out, halfadder_2_carry_out, halfadder_1_carry_out);
endmodule

module Mux_2_1 (
  input  a,
  input  b,
  input  sel,
  output S
);

  wire and_1_out, and_2_out, not_1_out;

  not not_1 (not_1_out, sel);
  and and_1 (and_1_out, a, not_1_out);
  and and_2 (and_2_out, sel, b);
  or or_1 (S, and_1_out, and_2_out);
endmodule

module Mux_4_1 (
  input  a,
  input  b,
  input  c,
  input  d,
  input  [1:0] sel1,
  output S
);

  wire mux_2_1_1_s, mux_2_1_2_s;

  Mux_2_1 mux_2_1_1 (.a(a), .b(b), .S(mux_2_1_1_s), .sel(sel1[0]));
  Mux_2_1 mux_2_1_2 (.a(c), .b(d), .S(mux_2_1_2_s), .sel(sel1[0]));
  Mux_2_1 mux_2_1_3 (.a(mux_2_1_1_s), .b(mux_2_1_2_s), .S(S), .sel(sel1[1]));
endmodule

module Mux_8_1 (
  input  in_1,
  input  in_2,
  input  in_3,
  input  in_4,
  input  in_5,
  input  in_6,
  input  in_7,
  input  in_8,
  input  [2:0] in_9,
  output out_10
);

  wire mux_4_1_1_s, mux_4_1_2_s;

  Mux_4_1 mux_4_1_1 (.a(in_1), .b(in_2), .c(in_3), .d(in_4), .S(mux_4_1_1_s), .sel1(in_9[1:0]));
  Mux_4_1 mux_4_1_2 (.a(in_5), .b(in_6), .c(in_7), .d(in_8), .S(mux_4_1_2_s), .sel1(in_9[1:0]));
  Mux_2_1 mux_2_1_1 (.a(mux_4_1_1_s), .b(mux_4_1_2_s), .S(out_10), .sel(in_9[2]));
endmodule

module PC (
  input  [3:0] In,
  output [3:0] out_2
);

  // Reg_4 reg_4_1: pin names not known; wires that end beside it: In, 1'b1, out_2
endmodule
