// Logisim project RegFile.circ as structural Verilog: 3 circuits, main circuit main
module main (
  input  [3:0] dIn,
  input  [3:0] XSel,
  input  [3:0] YSel,
  input  [3:0] wSel,
  output [3:0] XOut,
  output [3:0] YOut
);

  wire [3:0] reg_4_1_out_3, reg_4_2_out_3, reg_4_3_out_3, reg_4_4_out_3;

  Reg_4 reg_4_1 (.in_1(dIn), .in_2(wSel[3]), .out_3(reg_4_1_out_3));
  Reg_4 reg_4_2 (.in_1(dIn), .in_2(wSel[2]), .out_3(reg_4_2_out_3));
  Reg_4 reg_4_3 (.in_1(dIn), .in_2(wSel[1]), .out_3(reg_4_3_out_3));
  Reg_4 reg_4_4 (.in_1(dIn), .in_2(wSel[0]), .out_3(reg_4_4_out_3));
  Sel sel_1 (.A(reg_4_1_out_3), .B(reg_4_2_out_3), .C(reg_4_3_out_3), .D(reg_4_4_out_3), .Out(XOut), .Sel(XSel));
  Sel sel_2 (.A(reg_4_1_out_3), .B(reg_4_2_out_3), .C(reg_4_3_out_3), .D(reg_4_4_out_3), .Out(YOut), .Sel(YSel));
endmodule

module Sel (
  input  [3:0] A,
  input  [3:0] B,
  input  [3:0] C,
  input  [3:0] D,
  input  [3:0] Sel,
  output [3:0] Out
);

  wire [3:0] threestate4_1_out, threestate4_2_out, threestate4_3_out, threestate4_4_out;

  ThreeState4 threestate4_1 (.In(A), .Out(threestate4_1_out), .Sel(Sel[3]));
  ThreeState4 threestate4_2 (.In(B), .Out(threestate4_2_out), .Sel(Sel[2]));
  ThreeState4 threestate4_3 (.In(C), .Out(threestate4_3_out), .Sel(Sel[1]));
  ThreeState4 threestate4_4 (.In(D), .Out(threestate4_4_out), .Sel(Sel[0]));
  assign Out = threestate4_1_out | threestate4_2_out | threestate4_3_out | threestate4_4_out;  // OR_Gate or_1, 4 bits wide
endmodule

module dSel (
  input  [3:0] ALUIn,
  input  [3:0] RAMIn,
  input  Sel,
  output [3:0] Out
);

  Multiplexer #(.width(4), .enable("false")) multiplexer_1 (.in0(ALUIn), .in1(RAMIn), .out(Out), .sel(Sel));
endmodule
